# Fritzing sketch Electronique (saved by Fritzing 0.9.2b)

parts:
  U4 = HIH-4030 [package=hih-4030]
  U5 = HIH-4030 [package=hih-4030]
  U6 = LM2596 voltage regulator [package=sot23-5]
  Battery_12V_12Ah = Battery 12V 12Ah
  Joystick_Gauche = Thumb Joystick
  Joystick_Droit = Thumb Joystick
  LED1 = LED - 5mm [color="Red (633nm)" package="5 mm [THT]"]
  U7 = SWITCH_SPDT [package=kps-1290]
  LED2 = LEDs [package=led-0603]
  LED3 = LEDs [package=led-0603]
  Arduino_Mega_2560_rev3 = Arduino Mega 2560 (Rev3)
  M1 = DC Motor
  M2 = DC Motor
  M3 = DC Motor
  M4 = DC Motor
  U8 = L298 [package=multiwatt15]
  U9 = L298 [package=multiwatt15]
  U10 = L298 [package=multiwatt15]

nets:
  GND: U4.GND, U5.GND, U6.IN+, Battery_12V_12Ah.+, U8.CSA, U9.CSA, U10.CSA
  N1: U4.OUT, Arduino_Mega_2560_rev3.D24
  VCC: U4.VCC, U5.VCC, Arduino_Mega_2560_rev3.5V
  N2: U5.OUT, Arduino_Mega_2560_rev3.D25
  N3: U6.IN-, Battery_12V_12Ah.-
  VCC_2: U6.OUT+, Joystick_Gauche.VCC, Joystick_Droit.VCC, U7.P
  GND_2: U6.OUT-, Joystick_Gauche.GND, Joystick_Droit.GND, LED1.cathode, Arduino_Mega_2560_rev3.GND, U8.GND, U9.GND, U10.GND
  N4: Joystick_Gauche.SEL, Arduino_Mega_2560_rev3.A5
  N5: Joystick_Gauche.HORZ, Arduino_Mega_2560_rev3.A3
  N6: Joystick_Gauche.VERT, Arduino_Mega_2560_rev3.A4
  N7: Joystick_Droit.SEL, Arduino_Mega_2560_rev3.A2
  N8: Joystick_Droit.HORZ, Arduino_Mega_2560_rev3.A0
  N9: Joystick_Droit.VERT, Arduino_Mega_2560_rev3.A1
  N10: LED1.anode, Arduino_Mega_2560_rev3.A6
  N11: U7.S, Arduino_Mega_2560_rev3.VIN
  N12: LED2.A, U10.OUT2
  N13: LED2.C, U10.OUT1
  N14: LED3.A, U10.OUT4
  N15: LED3.C, U10.OUT3
  N16: Arduino_Mega_2560_rev3.D26, U8.IN4
  N17: Arduino_Mega_2560_rev3.D27, U8.IN3
  N18: Arduino_Mega_2560_rev3.D28, U8.IN2
  N19: Arduino_Mega_2560_rev3.D29, U8.IN1
  N20: Arduino_Mega_2560_rev3.D30, U9.IN4
  N21: Arduino_Mega_2560_rev3.D31, U9.IN3
  N22: Arduino_Mega_2560_rev3.D32, U9.IN2
  N23: Arduino_Mega_2560_rev3.D33, U9.IN1
  N24: Arduino_Mega_2560_rev3.D34, U10.IN4
  N25: Arduino_Mega_2560_rev3.D35, U10.IN3
  N26: Arduino_Mega_2560_rev3.D36, U10.IN2
  N27: Arduino_Mega_2560_rev3.D37, U10.IN1
  N28: M1.pin_1, U8.OUT3
  N29: M1.pin_2, U8.OUT4
  N30: M2.pin_1, U8.OUT1
  N31: M2.pin_2, U8.OUT2
  N32: M3.pin_1, U9.OUT3
  N33: M3.pin_2, U9.OUT4
  N34: M4.pin_1, U9.OUT1
  N35: M4.pin_2, U9.OUT2

custom parts:
  LM2596 voltage regulator: V_REG MIC5219 Standard 500mA LDO voltage regulator in SOT-23 layout. Micrel part MIC5219. BP (by-pass) pin is used to lower output noise with 470pF cap, may be left open.
